# Fritzing sketch joystick nRF24L circuit (saved by Fritzing 0.9.3b)

parts:
  부품1 = Arduino Uno (Rev3)
  부품2 = NRF24L01+ Breakout Board  # not connected
  부품3 = Thumb Joystick

nets:
  N1: 부품1.A0, 부품3.VERT
  N2: 부품1.A1, 부품3.HORZ
  GND: 부품1.GND, 부품3.GND
  5V: 부품1.5V, 부품3.VCC
